# Fritzing sketch 基本電路_ILI9341 (saved by Fritzing 0.9.2b)
breadboards: 1

parts:
  Ameba1 = Ameba
  TFT1 = Color 320x240 TFT Display, ILI9341 Controller Chip

nets:
  N1: Ameba1.D8, TFT1.Reset
  N2: Ameba1.D9, TFT1.D/C
  N3: Ameba1.D10, TFT1.CS
  N4: Ameba1.D11, TFT1.SDI_(MOSI)
  N5: Ameba1.D12, TFT1.SDO_(MISO)
  N6: Ameba1.D13, TFT1.SCK
  GND: Ameba1.GND, TFT1.GND
  3.3V: Ameba1.3.3V, TFT1.VCC, TFT1.LED

notes:
  電力請注意要接 3.3V
  Red Line: +3.3V
  Black Line: Gnd

custom parts:
  Ameba: Ameba EVB
  Color 320x240 TFT Display, ILI9341 Controller Chip: 2.2" TFT Display with ILI9341 Controller
