# Fritzing sketch 基本電路_Max7219_DotMatrix (saved by Fritzing 0.9.2b)
breadboards: 1

parts:
  Ameba1 = Ameba
  8x8_LED_Modul_mit_MAX1 = 8x8 LED Modul mit MAX7219 [package=THT]

nets:
  N1: Ameba1.D4, 8x8_LED_Modul_mit_MAX1.DIN_Eingang
  N2: Ameba1.D5, 8x8_LED_Modul_mit_MAX1.CS_Eingang
  N3: Ameba1.D6, 8x8_LED_Modul_mit_MAX1.CLK_Eingang
  N4: Ameba1.GND, 8x8_LED_Modul_mit_MAX1.GND_Eingang
  N5: Ameba1.5V, 8x8_LED_Modul_mit_MAX1.VCC_Eingang

custom parts:
  Ameba: Ameba EVB
