# Fritzing sketch 基本電路_Max7219_DotMatrix_X4 (saved by Fritzing 0.9.2b)
breadboards: 1

parts:
  Ameba1 = Ameba
  8x8_LED_Modul_mit_MAX1 = 8x8 LED Modul mit MAX7219 [package=THT]
  8x8_LED_Modul_mit_MAX2 = 8x8 LED Modul mit MAX7219 [package=THT]
  8x8_LED_Modul_mit_MAX3 = 8x8 LED Modul mit MAX7219 [package=THT]
  8x8_LED_Modul_mit_MAX4 = 8x8 LED Modul mit MAX7219 [package=THT]

nets:
  N1: Ameba1.D4, 8x8_LED_Modul_mit_MAX1.DIN_Eingang
  N2: Ameba1.D5, 8x8_LED_Modul_mit_MAX1.CS_Eingang
  N3: Ameba1.D6, 8x8_LED_Modul_mit_MAX1.CLK_Eingang
  N4: Ameba1.GND, 8x8_LED_Modul_mit_MAX1.GND_Eingang
  N5: Ameba1.5V, 8x8_LED_Modul_mit_MAX1.VCC_Eingang
  N6: 8x8_LED_Modul_mit_MAX1.VCC_Ausgang, 8x8_LED_Modul_mit_MAX2.VCC_Eingang
  N7: 8x8_LED_Modul_mit_MAX1.DOUT_Ausgang, 8x8_LED_Modul_mit_MAX2.DIN_Eingang
  N8: 8x8_LED_Modul_mit_MAX1.CS_Ausgang, 8x8_LED_Modul_mit_MAX2.CS_Eingang
  N9: 8x8_LED_Modul_mit_MAX1.CLK_Ausgang, 8x8_LED_Modul_mit_MAX2.CLK_Eingang
  N10: 8x8_LED_Modul_mit_MAX2.VCC_Ausgang, 8x8_LED_Modul_mit_MAX3.VCC_Eingang
  N11: 8x8_LED_Modul_mit_MAX2.GND_Ausgang, 8x8_LED_Modul_mit_MAX3.GND_Eingang
  N12: 8x8_LED_Modul_mit_MAX2.DOUT_Ausgang, 8x8_LED_Modul_mit_MAX3.DIN_Eingang
  N13: 8x8_LED_Modul_mit_MAX2.CS_Ausgang, 8x8_LED_Modul_mit_MAX3.CS_Eingang
  N14: 8x8_LED_Modul_mit_MAX2.CLK_Ausgang, 8x8_LED_Modul_mit_MAX3.CLK_Eingang
  N15: 8x8_LED_Modul_mit_MAX3.VCC_Ausgang, 8x8_LED_Modul_mit_MAX4.VCC_Eingang
  N16: 8x8_LED_Modul_mit_MAX3.GND_Ausgang, 8x8_LED_Modul_mit_MAX4.GND_Eingang
  N17: 8x8_LED_Modul_mit_MAX3.DOUT_Ausgang, 8x8_LED_Modul_mit_MAX4.DIN_Eingang
  N18: 8x8_LED_Modul_mit_MAX3.CS_Ausgang, 8x8_LED_Modul_mit_MAX4.CS_Eingang
  N19: 8x8_LED_Modul_mit_MAX3.CLK_Ausgang, 8x8_LED_Modul_mit_MAX4.CLK_Eingang

custom parts:
  Ameba: Ameba EVB
