# Fritzing sketch 基本電路_Nokia5110_ChitKit (saved by Fritzing 0.9.2b)
breadboards: 1

parts:
  Ameba1 = Ameba
  Nokia_5110_LCD_Module2 = Nokia5110LCDModule

nets:
  N1: Ameba1.D8, Nokia_5110_LCD_Module2.SCLK
  N2: Ameba1.D9, Nokia_5110_LCD_Module2.6_DN_(MOSI)
  N3: Ameba1.D10, Nokia_5110_LCD_Module2.D/C
  N4: Ameba1.D11, Nokia_5110_LCD_Module2.RST
  N5: Ameba1.D12, Nokia_5110_LCD_Module2.SCE
  N6: Ameba1.GND, Nokia_5110_LCD_Module2.Grnd
  5V: Ameba1.5V, Nokia_5110_LCD_Module2.Vcc
  N7: Ameba1.3.3V, Nokia_5110_LCD_Module2.LED

custom parts:
  Ameba: Ameba EVB
  : Nokia 5110 LCD with 8 pin. It's a 45mm*45mm module part. Description: The Nokia 5110 is a basic graphic LCD screen for lots of applications. It was originally intended for as a cell phone screen. This one is mounted on an easy to solder PCB. It uses the PCD8544 controller. The PCD8544 is a low power CMOS LCD controller/driver, designed to drive a graphic display of 48 rows and 84 columns. All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
