# Fritzing sketch 基本電路_OLED12864 (saved by Fritzing 0.9.2b)
breadboards: 1

parts:
  Ameba1 = Ameba
  Grove_OLED_Display_96x1 = Grove OLED Display 96x96

nets:
  N1: Ameba1.SCL, Grove_OLED_Display_96x1.SCL
  N2: Ameba1.SDA, Grove_OLED_Display_96x1.SDA
  GND: Ameba1.GND, Grove_OLED_Display_96x1.GND
  5V: Ameba1.5V, Grove_OLED_Display_96x1.VCC

notes:
  Oled 12864 Display
  Red: VCC(+5V)
  Black:Gnd
  Yellow:SDA(I2C Pin)
  Green:SCL(I2C Pin)

custom parts:
  Ameba: Ameba EVB
  Grove OLED Display 96x96: OLED Display 96x96, Grove connector.
