# Fritzing sketch 基本電路_將DHT溫度寫入FlashMemory (saved by Fritzing 0.9.2b)
breadboards: 1

parts:
  Ameba2 = Ameba
  DHT1 = DHT22 Humidity and Temperature Sensor

nets:
  GND: Ameba2.GND, DHT1.GND
  5V: Ameba2.5V, DHT1.VDD

notes:
  DHT 22
  Pin1 VCC
  Pin 2 Data
  Pin 3 N.C.
  Pin 4 GND

custom parts:
  Ameba: Ameba EVB
