# Fritzing sketch 基本電路_將光敏電阻值寫入FlashMemory (saved by Fritzing 0.9.2b)
breadboards: 1

parts:
  Ameba2 = Ameba
  R3 = Photocell (LDR) [package=THT]
  R4 = Resistor [tolerance=±5% resistance=4.7k package=THT]

nets:
  N1: Ameba2.A0, R3.pin_1, R4.Pin_1
  N2: Ameba2.GND, R3.pin_0
  N3: Ameba2.5V, R4.Pin_0

notes:
  光敏電阻量測電路
  4,7k Ω

custom parts:
  Ameba: Ameba EVB
