# Fritzing sketch 基本電路_DFPlayerMini (saved by Fritzing 0.9.2b)
breadboards: 1

parts:
  Ameba1 = Ameba
  DFPlayer_Mini1 = DFPlayer MINI [package="DIP (Dual Inline) [THT]"]
  SP1 = SPEAKER [package=pcb_mount_speaker]

nets:
  N1: Ameba1.D0, DFPlayer_Mini1.TX
  N2: Ameba1.D1, DFPlayer_Mini1.RX
  GND: Ameba1.GND, DFPlayer_Mini1.GND
  5V: Ameba1.5V, DFPlayer_Mini1.VCC
  N3: DFPlayer_Mini1.SPK1, SP1.-
  N4: DFPlayer_Mini1.SPK2, SP1.+

custom parts:
  Ameba: Ameba EVB
  DFPlayer MINI: MP3 module by DFRobot.com for playing Music from an SD-Card. Supports WAV and MP3 files.
