# Fritzing sketch 基本電路_DHT22 (saved by Fritzing 0.9.2b)
breadboards: 1

parts:
  Ameba1 = Ameba
  DHT3 = DHT22 Humidity and Temperature Sensor

nets:
  N1: Ameba1.D7, DHT3.DATA
  GND: Ameba1.GND, DHT3.GND
  5V: Ameba1.5V, DHT3.VDD

notes:
  DHT22
  Pin 1 ==>VCC
  Pin 2 ==>DataOut
  Pin 3 ==>No Used
  Pin 4 ==> GND

custom parts:
  Ameba: Ameba EVB
