# Fritzing sketch 基本電路_HC-SR04 (saved by Fritzing 0.9.2b)
breadboards: 1

parts:
  Ameba1 = Ameba
  Parte3 = SRF05 Ultrasonic Rangefinder
  R1 = Resistor [tolerance=±5% resistance=10k package=THT]
  R2 = Resistor [tolerance=±5% resistance=22k package=THT]

nets:
  5V: Ameba1.D12, Ameba1.5V, Parte3.VCC, Parte3.Trig
  N1: Ameba1.D13, R1.Pin_0, R2.Pin_1
  GND: Ameba1.GND, Parte3.Echo, Parte3.GND, R1.Pin_1, R2.Pin_0

custom parts:
  Ameba: Ameba EVB
