# Fritzing sketch 基本電路_LCD2004_按鈕開燈 (saved by Fritzing 0.9.2b)
breadboards: 1

parts:
  Ameba1 = Ameba
  LCM1602_IIC3 = LCM1602 IIC [part_number="LCM1602 IIC" chip_label="LCM1602 IIC" package="DIP (Dual Inline) [THT]"]
  LCD4 = LCD 20x04
  Grove1 = Grove Button
  R1 = Resistor [tolerance=±5% resistance=220 package=THT]
  LED1 = LED - 5mm [color="Red (633nm)" package="5 mm [THT]"]

nets:
  N1: Ameba1.D7, Grove1.SIG
  N2: Ameba1.D13, LED1.anode
  N3: Ameba1.SCL, LCM1602_IIC3.SCL
  N4: Ameba1.SDA, LCM1602_IIC3.SDA
  GND: Ameba1.GND, LCM1602_IIC3.GND, Grove1.GND, R1.Pin_0
  VCC: Ameba1.5V, LCM1602_IIC3.VCC, Grove1.VCC
  VSS: LCM1602_IIC3.VSS, LCD4.VSS
  VDD: LCM1602_IIC3.VDD, LCD4.VDD
  N5: LCM1602_IIC3.V0, LCD4.V0
  N6: LCM1602_IIC3.RS, LCD4.RS
  N7: LCM1602_IIC3.RW, LCD4.R/W
  N8: LCM1602_IIC3.E, LCD4.E
  N9: LCM1602_IIC3.D0, LCD4.DB0
  N10: LCM1602_IIC3.D1, LCD4.DB1
  N11: LCM1602_IIC3.D2, LCD4.DB2
  N12: LCM1602_IIC3.D3, LCD4.DB3
  N13: LCM1602_IIC3.D4, LCD4.DB4
  N14: LCM1602_IIC3.D5, LCD4.DB5
  N15: LCM1602_IIC3.D6, LCD4.DB6
  N16: LCM1602_IIC3.D7, LCD4.DB7
  N17: LCM1602_IIC3.A, LCD4.LED+
  N18: LCM1602_IIC3.K, LCD4.LED-
  N19: LCM1602_IIC3.LED_A, LCM1602_IIC3.LED_B
  N20: R1.Pin_1, LED1.cathode

notes:
  D13
  D7
  LED +5V
  D7
  GND
  LED GND
  220 Ω

custom parts:
  Ameba: Ameba EVB
  LCM1602 IIC: I2C-Module to use a 1602 or 2004 LCD on with the wire.h libory Serial LCD Modul
  LCD 20x04: LCD character display, 20 characters by 4 rows. Green.
