# Fritzing sketch 基本電路_PIR (saved by Fritzing 0.9.2b)
breadboards: 1

parts:
  Ameba1 = Ameba
  PIR2 = PIR sensor

nets:
  GND: Ameba1.GND, PIR2.GND
  5V: Ameba1.5V, PIR2.VDD, PIR2.SIG

custom parts:
  Ameba: Ameba EVB
